// Logisim project P0-L0-Q1.circ as structural Verilog: 3 circuits, main circuit CRC
module CRC_4bitMod2Div (
  input  [3:0] Diviend,
  input  [3:0] Divisor,
  output Quotient,
  output [2:0] Remainder
);

  wire [3:0] multiplexer_1_out;
  wire [3:3] xor_1_out;

  Multiplexer #(.width(4), .enable("false")) multiplexer_1 (
    .in0(4'b0000), .in1(Divisor), .out(multiplexer_1_out), .sel(Diviend[3]));
  assign {xor_1_out[3], Remainder} = Diviend ^ multiplexer_1_out;  // XOR_Gate xor_1, 4 bits wide

  assign Quotient = Diviend[3];
endmodule

module CRC_Mod2Div (
  input  [10:0] Diviend,
  input  [3:0] Divisor,
  output [7:0] Quotient,
  output [2:0] Remainder
);

  wire [2:0] crc_4bitmod2div_1_remainder, crc_4bitmod2div_2_remainder, crc_4bitmod2div_3_remainder,
       crc_4bitmod2div_4_remainder, crc_4bitmod2div_5_remainder, crc_4bitmod2div_6_remainder,
       crc_4bitmod2div_7_remainder;

  CRC_4bitMod2Div crc_4bitmod2div_1 (
    .Diviend(Diviend[10:7]), .Divisor(Divisor), .Quotient(Quotient[7]),
    .Remainder(crc_4bitmod2div_1_remainder));
  CRC_4bitMod2Div crc_4bitmod2div_2 (
    .Diviend({crc_4bitmod2div_1_remainder, Diviend[6]}), .Divisor(Divisor), .Quotient(Quotient[6]),
    .Remainder(crc_4bitmod2div_2_remainder));
  CRC_4bitMod2Div crc_4bitmod2div_3 (
    .Diviend({crc_4bitmod2div_2_remainder, Diviend[5]}), .Divisor(Divisor), .Quotient(Quotient[5]),
    .Remainder(crc_4bitmod2div_3_remainder));
  CRC_4bitMod2Div crc_4bitmod2div_4 (
    .Diviend({crc_4bitmod2div_3_remainder, Diviend[4]}), .Divisor(Divisor), .Quotient(Quotient[4]),
    .Remainder(crc_4bitmod2div_4_remainder));
  CRC_4bitMod2Div crc_4bitmod2div_5 (
    .Diviend({crc_4bitmod2div_4_remainder, Diviend[3]}), .Divisor(Divisor), .Quotient(Quotient[3]),
    .Remainder(crc_4bitmod2div_5_remainder));
  CRC_4bitMod2Div crc_4bitmod2div_6 (
    .Diviend({crc_4bitmod2div_5_remainder, Diviend[2]}), .Divisor(Divisor), .Quotient(Quotient[2]),
    .Remainder(crc_4bitmod2div_6_remainder));
  CRC_4bitMod2Div crc_4bitmod2div_7 (
    .Diviend({crc_4bitmod2div_6_remainder, Diviend[1]}), .Divisor(Divisor), .Quotient(Quotient[1]),
    .Remainder(crc_4bitmod2div_7_remainder));
  CRC_4bitMod2Div crc_4bitmod2div_8 (
    .Diviend({crc_4bitmod2div_7_remainder, Diviend[0]}), .Divisor(Divisor), .Quotient(Quotient[0]),
    .Remainder(Remainder));

  // Other names for the same wires on the sheet: d6 = Diviend[6]; d5 = Diviend[5]; d4 = Diviend[4]; d3 = Diviend[3];
  //   d2 = Diviend[2]; d1 = Diviend[1]; d0 = Diviend[0]; q0 = Quotient[0]; q1 = Quotient[1]; q2 = Quotient[2];
  //   q3 = Quotient[3]; q4 = Quotient[4]; q5 = Quotient[5]; q6 = Quotient[6]; q7 = Quotient[7]
endmodule

module CRC (
  input  [7:0] A,
  input  [3:0] B,
  output [10:0] C
);

  CRC_Mod2Div crc_mod2div_1 (.Diviend({A, 3'b000}), .Divisor(B), .Remainder(C[2:0]));  // open: Quotient

  assign C[10:3] = A;
endmodule
