// Logisim project P0-L0-Q3-check.circ as structural Verilog: 2 circuits, main circuit test_GRF
module test_GRF (
  input  clear,
  input  clear_2
);

  wire clk, clock_1_out, comparator_1_eq, comparator_2_eq, counter_2_carry, counter_3_q, counter_4_carry,
       not_1_out, not_2_out, not_3_out, not_4_out, not_5_out, s_r_ff_1_q, s_r_ff_2_q;
  wire [1:0] counter_2_q;
  wire [4:0] counter_4_q, counter_5_q, subtractor_1_out;
  wire [31:0] counter_1_q, dummy_grf_1_rd1, dummy_grf_1_rd2, dummy_grf_2_rd1, dummy_grf_2_rd2, WD;

  not not_1 (not_1_out, s_r_ff_2_q);
  Clock clock_1 (.out(clock_1_out));
  not not_2 (not_2_out, s_r_ff_1_q);
  Counter #(.width(32), .max('hffffffff)) counter_1 (.Q(counter_1_q), .clk(clk));  // open: load, D, count, carry, clr
  and and_1 (clk, not_1_out, not_2_out, clock_1_out, not_3_out);
  not not_3 (not_3_out, counter_2_carry);
  Multiplexer #(.select(2), .width(32), .enable("false")) multiplexer_1 (
    .in0(counter_1_q), .in1(32'hff30c21b), .in2({32{1'b0}}), .out(WD), .sel(counter_2_q));  // open: in3
  Counter #(.width(2), .max('h3)) counter_2 (
    .Q(counter_2_q), .carry(counter_2_carry), .clk(counter_4_carry));  // open: load, D, count, clr
  Counter #(.width(1), .max('h1)) counter_3 (.Q(counter_3_q), .clk(clk));  // open: load, D, count, carry, clr
  Subtractor #(.width(5)) subtractor_1 (.a(counter_5_q), .b(5'b00001), .out(subtractor_1_out));  // open: bin, bout
  Counter #(.width(5), .max('h1f)) counter_4 (
    .Q(counter_4_q), .carry(counter_4_carry), .clk(clk));  // open: load, D, count, clr
  Counter #(.width(5), .max('h1f)) counter_5 (.Q(counter_5_q), .clk(clk));  // open: load, D, count, carry, clr
  dummy_grf dummy_grf_1 (
    .A1(subtractor_1_out), .A2(counter_4_q), .A3(counter_5_q), .WD(WD), .clk(clk), .reset(clear),
    .WE(counter_3_q), .RD1(dummy_grf_1_rd1), .RD2(dummy_grf_1_rd2));
  dummy_grf dummy_grf_2 (
    .A1(subtractor_1_out), .A2(counter_4_q), .A3(counter_4_q), .WD(WD), .clk(clk), .reset(clear_2),
    .WE(counter_3_q), .RD1(dummy_grf_2_rd1), .RD2(dummy_grf_2_rd2));
  Comparator #(.width(32), .mode("unsigned")) comparator_1 (
    .a(dummy_grf_1_rd2), .b(dummy_grf_2_rd2), .eq(comparator_1_eq));  // open: gt, lt
  Comparator #(.width(32), .mode("unsigned")) comparator_2 (
    .a(dummy_grf_1_rd1), .b(dummy_grf_2_rd1), .eq(comparator_2_eq));  // open: gt, lt
  not not_4 (not_4_out, comparator_1_eq);
  S_R_Flip_Flop s_r_ff_1 (.S(not_5_out), .clk(clk), .R(1'b0), .Q(s_r_ff_1_q), .en(1'b1));  // open: Qn, preset, reset
  not not_5 (not_5_out, comparator_2_eq);
  S_R_Flip_Flop s_r_ff_2 (.S(not_4_out), .clk(clk), .R(1'b0), .Q(s_r_ff_2_q), .en(1'b1));  // open: Qn, preset, reset
  LED led_1 (.in(s_r_ff_1_q));
  LED led_2 (.in(s_r_ff_2_q));
endmodule

module dummy_grf (
  input  clk,
  input  reset,
  input  WE,
  input  [4:0] A1,
  input  [4:0] A2,
  input  [4:0] A3,
  input  [31:0] WD,
  output [31:0] RD1,
  output [31:0] RD2
);
endmodule
