// Logisim project P0-L0-Q4.circ as structural Verilog: 3 circuits, main circuit fsm
module fsm (
  input  CLR,
  input  [1:0] In,
  output Z
);

  wire clock_1_out;
  wire [1:0] multiplexer_1_out, register_1_q, state_1_nextstate;

  Multiplexer #(.width(2), .enable("false")) multiplexer_1 (
    .in0(state_1_nextstate), .in1(2'b00), .out(multiplexer_1_out), .sel(CLR));
  State state_1 (.In(In), .CurrentState(register_1_q), .NextState(state_1_nextstate));
  Register #(.width(2)) register_1 (.D(multiplexer_1_out), .Q(register_1_q), .clk(clock_1_out));  // open: en, clr
  Clock clock_1 (.out(clock_1_out));
  Output output_1 (.State(register_1_q), .In(In), .Z(Z));
endmodule

module State (
  input  [1:0] In,
  input  [1:0] CurrentState,
  output [1:0] NextState
);

  wire not_1_out, not_2_out;

  not not_1 (not_1_out, In[0]);
  not not_2 (not_2_out, In[1]);
  and and_1 (NextState[1], not_1_out, CurrentState[0]);
  and and_2 (NextState[0], not_2_out, In[0]);
endmodule

module Output (
  input  [1:0] State,
  input  [1:0] In,
  output Z
);

  wire not_1_out;

  not not_1 (not_1_out, In[0]);
  and and_1 (Z, State[1], not_1_out);
endmodule
