// Logisim project P0-L0-Q4-check.circ as structural Verilog: 2 circuits, main circuit test
module test (
  input  clr,
  input  Override
);

  wire and_1_out, clock_1_out, comparator_1_eq, comparator_2_eq, counter_1_carry, counter_2_carry,
       counter_3_carry, counter_4_carry, counter_5_carry, counter_6_carry, counter_7_carry, dummy_fsm_1_z,
       dummy_fsm_2_z, multiplexer_1_out, not_1_out, not_2_out, not_3_out, s_r_ff_1_q;
  wire [1:0] counter_2_q, counter_3_q, counter_4_q, counter_5_q, counter_6_q, counter_7_q, In;
  wire [2:0] counter_1_q;
  wire [5:0] random_1_out;

  Clock clock_1 (.out(clock_1_out));
  not not_1 (not_1_out, s_r_ff_1_q);
  not not_2 (not_2_out, counter_7_carry);
  Random #(.width(6)) random_1 (.clk(and_1_out), .out(random_1_out));  // open: next, clr
  and and_1 (and_1_out, clock_1_out, not_1_out, not_2_out);
  Comparator #(.width(6), .mode("unsigned")) comparator_1 (
    .a(random_1_out), .b({6{1'b1}}), .eq(comparator_1_eq));  // open: gt, lt
  Multiplexer #(.enable("false")) multiplexer_1 (
    .in0(comparator_1_eq), .in1(clr), .out(multiplexer_1_out), .sel(Override));
  Counter #(.width(3), .max('h7)) counter_1 (
    .Q(counter_1_q), .carry(counter_1_carry), .clk(and_1_out));  // open: load, D, count, clr
  dummy_fsm dummy_fsm_1 (.CLR(multiplexer_1_out), .In(In), .Z(dummy_fsm_1_z));
  dummy_fsm dummy_fsm_2 (.CLR(multiplexer_1_out), .In(In), .Z(dummy_fsm_2_z));
  Counter #(.width(2), .max('h3)) counter_2 (
    .Q(counter_2_q), .carry(counter_2_carry), .clk(counter_3_carry));  // open: load, D, count, clr
  Counter #(.width(2), .max('h3)) counter_3 (
    .Q(counter_3_q), .carry(counter_3_carry), .clk(counter_1_carry));  // open: load, D, count, clr
  Comparator #(.width(1), .mode("unsigned")) comparator_2 (
    .a(dummy_fsm_1_z), .b(dummy_fsm_2_z), .eq(comparator_2_eq));  // open: gt, lt
  Multiplexer #(.select(3), .width(2), .enable("false")) multiplexer_2 (
    .in0(counter_3_q), .in1(counter_2_q), .in2(counter_4_q), .in3(counter_5_q), .in4(counter_6_q),
    .in5(counter_7_q), .in6(2'b11), .in7(2'b11), .out(In), .sel(counter_1_q));
  Counter #(.width(2), .max('h3)) counter_4 (
    .Q(counter_4_q), .carry(counter_4_carry), .clk(counter_2_carry));  // open: load, D, count, clr
  not not_3 (not_3_out, comparator_2_eq);
  Counter #(.width(2), .max('h3)) counter_5 (
    .Q(counter_5_q), .carry(counter_5_carry), .clk(counter_4_carry));  // open: load, D, count, clr
  Counter #(.width(2), .max('h3)) counter_6 (
    .Q(counter_6_q), .carry(counter_6_carry), .clk(counter_5_carry));  // open: load, D, count, clr
  S_R_Flip_Flop s_r_ff_1 (
    .S(not_3_out), .clk(and_1_out), .R(1'b0), .Q(s_r_ff_1_q), .en(1'b1));  // open: Qn, preset, reset
  Counter #(.width(2), .max('h3)) counter_7 (
    .Q(counter_7_q), .carry(counter_7_carry), .clk(counter_6_carry));  // open: load, D, count, clr
  LED led_1 (.in(s_r_ff_1_q));
endmodule

module dummy_fsm (
  input  CLR,
  input  [1:0] In,
  output Z
);
endmodule
