// Logisim project CPU - With JAL.circ as structural Verilog: 13 circuits, main circuit GRF
module GRF (
  input  clk,
  input  reset,
  input  RegWEnable,
  input  [4:0] RAddr1,
  input  [4:0] RAddr2,
  input  [4:0] RegWAddr,
  input  [31:0] RegWData,
  output [31:0] RD1,
  output [31:0] RD2
);

  wire we0, we1, we2, we3, we4, we5, we6, we7, we8, we9, we10, we11, we12, we13, we14, we15, we16, we17,
       we18, we19, we20, we21, we22, we23, we24, we25, we26, we27, we28, we29, we30, we31;
  wire [31:0] out0, out1, out2, out3, out4, out5, out6, out7, out8, out9, out10, out11, out12, out13, out14,
       out15, out16, out17, out18, out19, out20, out21, out22, out23, out24, out25, out26, out27, out28,
       out29, out30, out31;

  Decoder #(.select(5), .disabled(0)) decoder_1 (
    .out0(we0), .out1(we1), .out2(we2), .out3(we3), .out4(we4), .out5(we5), .out6(we6), .out7(we7),
    .out8(we8), .out9(we9), .out10(we10), .out11(we11), .out12(we12), .out13(we13), .out14(we14),
    .out15(we15), .out16(we16), .out17(we17), .out18(we18), .out19(we19), .out20(we20), .out21(we21),
    .out22(we22), .out23(we23), .out24(we24), .out25(we25), .out26(we26), .out27(we27), .out28(we28),
    .out29(we29), .out30(we30), .out31(we31), .sel(RegWAddr), .en(RegWEnable));
  Register #(.width(32)) register_1 (.D({32{1'b0}}), .en(we0), .Q(out0), .clk(clk), .clr(reset));
  Register #(.width(32)) register_2 (.D(RegWData), .en(we7), .Q(out7), .clk(clk), .clr(reset));
  Register #(.width(32)) register_3 (.D(RegWData), .en(we14), .Q(out14), .clk(clk), .clr(reset));
  Register #(.width(32)) register_4 (.D(RegWData), .en(we21), .Q(out21), .clk(clk), .clr(reset));
  Register #(.width(32)) register_5 (.D(RegWData), .en(we28), .Q(out28), .clk(clk), .clr(reset));
  Register #(.width(32)) register_6 (.D(RegWData), .en(we1), .Q(out1), .clk(clk), .clr(reset));
  Register #(.width(32)) register_7 (.D(RegWData), .en(we8), .Q(out8), .clk(clk), .clr(reset));
  Register #(.width(32)) register_8 (.D(RegWData), .en(we15), .Q(out15), .clk(clk), .clr(reset));
  Register #(.width(32)) register_9 (.D(RegWData), .en(we22), .Q(out22), .clk(clk), .clr(reset));
  Register #(.width(32)) register_10 (.D(RegWData), .en(we29), .Q(out29), .clk(clk), .clr(reset));
  Multiplexer #(.select(5), .width(32), .enable("false")) multiplexer_1 (
    .in0(out0), .in1(out1), .in2(out2), .in3(out3), .in4(out4), .in5(out5), .in6(out6), .in7(out7),
    .in8(out8), .in9(out9), .in10(out10), .in11(out11), .in12(out12), .in13(out13), .in14(out14),
    .in15(out15), .in16(out16), .in17(out17), .in18(out18), .in19(out19), .in20(out20), .in21(out21),
    .in22(out22), .in23(out23), .in24(out24), .in25(out25), .in26(out26), .in27(out27), .in28(out28),
    .in29(out29), .in30(out30), .in31(out31), .out(RD2), .sel(RAddr2));
  Register #(.width(32)) register_11 (.D(RegWData), .en(we2), .Q(out2), .clk(clk), .clr(reset));
  Register #(.width(32)) register_12 (.D(RegWData), .en(we9), .Q(out9), .clk(clk), .clr(reset));
  Register #(.width(32)) register_13 (.D(RegWData), .en(we16), .Q(out16), .clk(clk), .clr(reset));
  Register #(.width(32)) register_14 (.D(RegWData), .en(we23), .Q(out23), .clk(clk), .clr(reset));
  Register #(.width(32)) register_15 (.D(RegWData), .en(we30), .Q(out30), .clk(clk), .clr(reset));
  Register #(.width(32)) register_16 (.D(RegWData), .en(we3), .Q(out3), .clk(clk), .clr(reset));
  Register #(.width(32)) register_17 (.D(RegWData), .en(we10), .Q(out10), .clk(clk), .clr(reset));
  Register #(.width(32)) register_18 (.D(RegWData), .en(we17), .Q(out17), .clk(clk), .clr(reset));
  Register #(.width(32)) register_19 (.D(RegWData), .en(we24), .Q(out24), .clk(clk), .clr(reset));
  Register #(.width(32)) register_20 (.D(RegWData), .en(we31), .Q(out31), .clk(clk), .clr(reset));
  Multiplexer #(.select(5), .width(32), .enable("false")) multiplexer_2 (
    .in0(out0), .in1(out1), .in2(out2), .in3(out3), .in4(out4), .in5(out5), .in6(out6), .in7(out7),
    .in8(out8), .in9(out9), .in10(out10), .in11(out11), .in12(out12), .in13(out13), .in14(out14),
    .in15(out15), .in16(out16), .in17(out17), .in18(out18), .in19(out19), .in20(out20), .in21(out21),
    .in22(out22), .in23(out23), .in24(out24), .in25(out25), .in26(out26), .in27(out27), .in28(out28),
    .in29(out29), .in30(out30), .in31(out31), .out(RD1), .sel(RAddr1));
  Register #(.width(32)) register_21 (.D(RegWData), .en(we4), .Q(out4), .clk(clk), .clr(reset));
  Register #(.width(32)) register_22 (.D(RegWData), .en(we11), .Q(out11), .clk(clk), .clr(reset));
  Register #(.width(32)) register_23 (.D(RegWData), .en(we18), .Q(out18), .clk(clk), .clr(reset));
  Register #(.width(32)) register_24 (.D(RegWData), .en(we25), .Q(out25), .clk(clk), .clr(reset));
  Register #(.width(32)) register_25 (.D(RegWData), .en(we5), .Q(out5), .clk(clk), .clr(reset));
  Register #(.width(32)) register_26 (.D(RegWData), .en(we12), .Q(out12), .clk(clk), .clr(reset));
  Register #(.width(32)) register_27 (.D(RegWData), .en(we19), .Q(out19), .clk(clk), .clr(reset));
  Register #(.width(32)) register_28 (.D(RegWData), .en(we26), .Q(out26), .clk(clk), .clr(reset));
  Register #(.width(32)) register_29 (.D(RegWData), .en(we6), .Q(out6), .clk(clk), .clr(reset));
  Register #(.width(32)) register_30 (.D(RegWData), .en(we13), .Q(out13), .clk(clk), .clr(reset));
  Register #(.width(32)) register_31 (.D(RegWData), .en(we20), .Q(out20), .clk(clk), .clr(reset));
  Register #(.width(32)) register_32 (.D(RegWData), .en(we27), .Q(out27), .clk(clk), .clr(reset));

  // Other names for the same wires on the sheet: A1[4:0] = RAddr1; A2[4:0] = RAddr2; A3[4:0] = RegWAddr;
  //   WD[31:0] = RegWData; WE = RegWEnable
endmodule

module main (
  input  reset,
  output [31:0] Instr,
  output RegWrite,
  output [4:0] RegAddr,
  output [31:0] RegData,
  output MemWrite,
  output [4:0] MemAddr,
  output [31:0] MemData
);

  CPU cpu_1 (
    .reset(reset), .Instr(Instr), .RegWrite(RegWrite), .RegAddr(RegAddr), .RegData(RegData),
    .MemWrite(MemWrite), .MemAddr(MemAddr), .MemData(MemData));
endmodule

module DM (
  input  clk,
  input  reset,
  input  MemWEnable,
  input  [31:0] Address,
  input  [31:0] MemWData,
  input  [1:0] MemMode,
  output [31:0] MemRData
);

  wire [7:0] bit_extender_2_out, bit_extender_6_out, bitselector_2_out;
  wire [15:0] bit_extender_1_out, bit_extender_3_out, bitselector_1_out;
  wire [31:0] and_1_out, bit_extender_4_out, bit_extender_5_out, bit_extender_7_out, bit_extender_8_out,
       bit_extender_9_out, bit_extender_10_out, memword, memwritemask, memwritetmp, multiplexer_2_out,
       or_1_out, shifter_1_out, shifter_2_out, shifter_3_out, shifter_4_out;

  Bit_Extender #(.in_width(32)) bit_extender_1 (.in(MemWData), .out(bit_extender_1_out));
  Bit_Extender #(.in_width(32), .out_width(8)) bit_extender_2 (.in(MemWData), .out(bit_extender_2_out));
  Bit_Extender #(.in_width(32)) bit_extender_3 (.in({32{1'b1}}), .out(bit_extender_3_out));
  assign bit_extender_4_out = {{16{1'b0}}, bit_extender_3_out};  // Bit_Extender bit_extender_4
  assign bit_extender_5_out = {{24{1'b0}}, bit_extender_6_out};  // Bit_Extender bit_extender_5
  Bit_Extender #(.in_width(32), .out_width(8)) bit_extender_6 (.in({32{1'b1}}), .out(bit_extender_6_out));
  assign bit_extender_7_out = {{16{1'b0}}, bit_extender_1_out};  // Bit_Extender bit_extender_7
  assign bit_extender_8_out = {{24{1'b0}}, bit_extender_2_out};  // Bit_Extender bit_extender_8
  assign and_1_out = memwritemask & memword;  // AND_Gate and_1, 32 bits wide
  Shifter #(.width(32)) shifter_1 (.in(bit_extender_7_out), .\dist ({Address[0], 4'b0000}), .out(shifter_1_out));
  Shifter #(.width(32)) shifter_2 (.in(bit_extender_8_out), .\dist ({Address[1:0], 3'b000}), .out(shifter_2_out));
  Shifter #(.width(32)) shifter_3 (.in(bit_extender_4_out), .\dist ({Address[0], 4'b0000}), .out(shifter_3_out));
  Shifter #(.width(32)) shifter_4 (.in(bit_extender_5_out), .\dist ({Address[1:0], 3'b000}), .out(shifter_4_out));
  assign or_1_out = and_1_out | memwritetmp;  // OR_Gate or_1, 32 bits wide
  Multiplexer #(.select(2), .width(32), .enable("false")) multiplexer_1 (
    .in0(MemWData), .in1(shifter_1_out), .in3(shifter_2_out), .out(memwritetmp), .sel(MemMode));  // open: in2
  Multiplexer #(.select(2), .width(32), .enable("false")) multiplexer_2 (
    .in0({32{1'b1}}), .in1(shifter_3_out), .in3(shifter_4_out), .out(multiplexer_2_out), .sel(MemMode));  // open: in2
  assign memwritemask = ~multiplexer_2_out;  // NOT_Gate not_1, 32 bits wide
  RAM #(.addrWidth(5), .dataWidth(32), .bus("separate")) ram_1 (
    .addr(Address[6:2]), .din(or_1_out), .data(memword), .str(MemWEnable), .sel(1'b1), .clk(clk), .clr(reset));  // open: ld
  BitSelector #(.width(32), .group(16)) bitselector_1 (.in(memword), .out(bitselector_1_out), .sel(Address[0]));
  BitSelector #(.width(32), .group(8)) bitselector_2 (.in(memword), .out(bitselector_2_out), .sel(Address[1:0]));
  assign bit_extender_9_out = {{16{bitselector_1_out[15]}}, bitselector_1_out};  // Bit_Extender bit_extender_9
  assign bit_extender_10_out = {{24{bitselector_2_out[7]}}, bitselector_2_out};  // Bit_Extender bit_extender_10
  Multiplexer #(.select(2), .width(32), .enable("false")) multiplexer_3 (
    .in0(memword), .in1(bit_extender_9_out), .in3(bit_extender_10_out), .out(MemRData), .sel(MemMode));  // open: in2

  // Other names for the same wires on the sheet: addr0 = Address[0]; addr1 = Address[1]

  // Notes on the sheet:
  //   符号延拓，可设置
endmodule

module IFU (
  input  clk,
  input  reset,
  input  JumpReg,
  input  Jump,
  input  Branch,
  input  [15:0] branchOffset,
  input  [25:0] JAddress,
  input  [31:0] JRAddress,
  output [31:0] Instr,
  output [31:0] PC_4
);

  wire [31:0] adder_2_out, branchOffset_t, JAddress_t, multiplexer_1_out, multiplexer_2_out,
       multiplexer_3_out, register_1_q, shifter_1_out, shifter_2_out;

  assign branchOffset_t = {{16{branchOffset[15]}}, branchOffset};  // Bit_Extender bit_extender_1
  assign JAddress_t = {{6{1'b0}}, JAddress};  // Bit_Extender bit_extender_2
  Register #(.width(32)) register_1 (.D(multiplexer_3_out), .Q(register_1_q), .clk(clk), .clr(reset));  // open: en
  Adder #(.width(32)) adder_1 (.a(32'h4), .b(register_1_q), .out(PC_4));  // open: cin, cout
  Shifter #(.width(32)) shifter_1 (.in(branchOffset_t), .\dist (5'b00010), .out(shifter_1_out));
  Adder #(.width(32)) adder_2 (.a(PC_4), .b(shifter_1_out), .out(adder_2_out));  // open: cin, cout
  ROM #(.addrWidth(5), .dataWidth(32)) rom_1 (.addr(register_1_q[6:2]), .data(Instr));  // open: sel
  Multiplexer #(.width(32), .enable("false")) multiplexer_1 (
    .in0(PC_4), .in1(adder_2_out), .out(multiplexer_1_out), .sel(Branch));
  Shifter #(.width(32)) shifter_2 (.in(JAddress_t), .\dist (5'b00010), .out(shifter_2_out));
  Multiplexer #(.width(32), .enable("false")) multiplexer_2 (
    .in0(multiplexer_1_out), .in1({multiplexer_1_out[31:28], shifter_2_out[27:0]}), .out(multiplexer_2_out),
    .sel(Jump));
  Multiplexer #(.width(32), .enable("false")) multiplexer_3 (
    .in0(multiplexer_2_out), .in1(JRAddress), .out(multiplexer_3_out), .sel(JumpReg));

  // Notes on the sheet:
  //   contents of rom_1 (hex, n*v repeats v):
  //   3c00000a 3c010000 3c020000 3c030000 3c040000 34420001 34840007 3c050000 34a50020 3c060000 34c60004
  //   c00000d c000016 10830006 621821 a62823 acbf0000 c00000d 8cbf0000 a62821 3e00008 3c101234 3c0f7890
endmodule

module ALU (
  input  [31:0] Operand1,
  input  [31:0] Operand2,
  input  [2:0] ALUOperation,
  output [31:0] Result,
  output isZero
);

  wire [31:0] adder_1_out, or_1_out, subtractor_1_out;

  Adder #(.width(32)) adder_1 (.a(Operand2), .b(Operand1), .out(adder_1_out), .cin(1'b0));  // open: cout
  Subtractor #(.width(32)) subtractor_1 (.a(Operand1), .b(Operand2), .out(subtractor_1_out));  // open: bin, bout
  assign or_1_out = Operand1 | Operand2;  // OR_Gate or_1, 32 bits wide
  Multiplexer #(.select(3), .width(32), .enable("false")) multiplexer_1 (
    .in0(adder_1_out), .in1(subtractor_1_out), .in2(or_1_out), .out(Result), .sel(ALUOperation));  // open: in3, in4, in5, in6, in7
  Comparator #(.width(32)) comparator_1 (.a(Result), .b({32{1'b0}}), .eq(isZero));  // open: gt, lt
endmodule

module EXT (
  input  [15:0] EXTInput,
  input  EXTMode,
  output [31:0] EXTOutput
);

  wire [31:0] bit_extender_1_out, bit_extender_2_out;

  assign bit_extender_1_out = {{16{1'b0}}, EXTInput};  // Bit_Extender bit_extender_1
  assign bit_extender_2_out = {{16{EXTInput[15]}}, EXTInput};  // Bit_Extender bit_extender_2
  Multiplexer #(.width(32), .enable("false")) multiplexer_1 (
    .in0(bit_extender_1_out), .in1(bit_extender_2_out), .out(EXTOutput), .sel(EXTMode));
endmodule

module RegWAddrpath (
  input  [1:0] RegWAddrpath_sel,
  input  [4:0] RegWAddrpath_rdIn,
  input  [4:0] RegWAddrpath_rtIn,
  input  [4:0] RegWAddrpath_pcIn,
  output [4:0] RegWAddrpath_out
);

  Multiplexer #(.select(2), .width(5), .enable("false")) multiplexer_1 (
    .in0(RegWAddrpath_rdIn), .in1(RegWAddrpath_rtIn), .in2(RegWAddrpath_pcIn), .out(RegWAddrpath_out),
    .sel(RegWAddrpath_sel));  // open: in3
endmodule

module RegWDatapath (
  input  [1:0] RegWDatapath_sel,
  input  [31:0] RegWDatapath_aluIn,
  input  [31:0] RegWDatapath_memIn,
  input  [31:0] RegWDatapath_pcIn,
  output [31:0] RegWDatapath_out
);

  Multiplexer #(.select(2), .width(32), .disabled(0), .enable("false")) multiplexer_1 (
    .in0(RegWDatapath_aluIn), .in1(RegWDatapath_memIn), .in2(RegWDatapath_pcIn), .out(RegWDatapath_out),
    .sel(RegWDatapath_sel));  // open: in3
endmodule

module ALUOp2Datapath (
  input  [1:0] ALUOp2Datapath_sel,
  input  [31:0] ALUOp2Datapath_regIn,
  input  [31:0] ALUOp2Datapath_extIn,
  input  [31:0] ALUOp2Datapath_shiftIn,
  output [31:0] ALUOp2Datapath_out
);

  Multiplexer #(.select(2), .width(32), .enable("false")) multiplexer_1 (
    .in0(ALUOp2Datapath_regIn), .in1(ALUOp2Datapath_extIn), .in2(ALUOp2Datapath_shiftIn),
    .out(ALUOp2Datapath_out), .sel(ALUOp2Datapath_sel));  // open: in3
endmodule

module InstructionDecoder (
  input  OpCode5,
  input  OpCode4,
  input  OpCode3,
  input  OpCode2,
  input  OpCode1,
  input  OpCode0,
  input  Funct5,
  input  Funct4,
  input  Funct3,
  input  Funct2,
  input  Funct1,
  input  Funct0,
  output ID_addu,
  output ID_subu,
  output ID_ori,
  output ID_lw,
  output ID_sw,
  output ID_beq,
  output ID_lui,
  output ID_jal,
  output ID_jr
);

  wire funct0_0, funct1_0, funct2_0, funct3_0, funct4_0, funct5_0, op0_0, op1_0, op2_0, op3_0, op4_0, op5_0,
       TypeR;

  not not_1 (op5_0, OpCode5);
  not not_2 (op4_0, OpCode4);
  not not_3 (op3_0, OpCode3);
  not not_4 (op2_0, OpCode2);
  not not_5 (op1_0, OpCode1);
  not not_6 (op0_0, OpCode0);
  not not_7 (funct5_0, Funct5);
  not not_8 (funct4_0, Funct4);
  not not_9 (funct3_0, Funct3);
  not not_10 (funct2_0, Funct2);
  not not_11 (funct1_0, Funct1);
  not not_12 (funct0_0, Funct0);
  and and_1 (TypeR, op5_0, op4_0, op3_0, op2_0, op1_0, op0_0);
  and and_2 (ID_subu, TypeR, Funct5, funct4_0, funct3_0, funct2_0, Funct1, Funct0);
  and and_3 (ID_lw, OpCode5, op4_0, op3_0, op2_0, OpCode1, OpCode0);
  and and_4 (ID_beq, op5_0, op4_0, op3_0, OpCode2, op1_0, op0_0);
  and and_5 (ID_jal, op5_0, op4_0, op3_0, op2_0, OpCode1, OpCode0);
  and and_6 (ID_addu, TypeR, Funct5, funct4_0, funct3_0, funct2_0, funct1_0, Funct0);
  and and_7 (ID_ori, op5_0, op4_0, OpCode3, OpCode2, op1_0, OpCode0);
  and and_8 (ID_sw, OpCode5, op4_0, OpCode3, op2_0, OpCode1, OpCode0);
  and and_9 (ID_lui, op5_0, op4_0, OpCode3, OpCode2, OpCode1, OpCode0);
  and and_10 (ID_jr, TypeR, funct5_0, funct4_0, Funct3, funct2_0, funct1_0, funct0_0);

  // Other names for the same wires on the sheet: addu = ID_addu; beq = ID_beq; funct0_1 = Funct0; funct1_1 = Funct1;
  //   funct2_1 = Funct2; funct3_1 = Funct3; funct4_1 = Funct4; funct5_1 = Funct5; jal = ID_jal; jr = ID_jr;
  //   lui = ID_lui; lw = ID_lw; op0_1 = OpCode0; op1_1 = OpCode1; op2_1 = OpCode2; op3_1 = OpCode3; op4_1 = OpCode4;
  //   op5_1 = OpCode5; ori = ID_ori; subu = ID_subu; sw = ID_sw
endmodule

module ControlSignalGenerator (
  input  ID_addu,
  input  ID_subu,
  input  ID_ori,
  input  ID_lw,
  input  ID_sw,
  input  ID_beq,
  input  ID_lui,
  input  ID_jal,
  input  ID_jr,
  output BranchEqual,
  output Jump,
  output RegWEnable,
  output [1:0] RegWAddrpath_sel,
  output [1:0] RegWDatapath_sel,
  output [2:0] ALUOperation,
  output [1:0] ALUOp2Datapath_sel,
  output MemWEnable,
  output [1:0] MemMode,
  output EXTMode,
  output Link,
  output JumpReg
);

  or or_1 (BranchEqual, 1'b0, ID_beq);
  or or_2 (Jump, 1'b0, ID_jal);
  or or_3 (RegWEnable, 1'b0, ID_addu, ID_subu, ID_ori, ID_lw, ID_lui, ID_jal);
  or or_4 (RegWAddrpath_sel[1], 1'b0, ID_jal);
  or or_5 (RegWAddrpath_sel[0], 1'b0, ID_ori, ID_lw, ID_lui);
  or or_6 (RegWDatapath_sel[1], 1'b0, ID_jal);
  or or_7 (RegWDatapath_sel[0], 1'b0, ID_lw);
  buf or_8 (ALUOperation[2], 1'b0);  // OR_Gate
  or or_9 (ALUOperation[1], 1'b0, ID_lui, ID_ori);
  or or_10 (ALUOperation[0], 1'b0, ID_subu, ID_beq);
  or or_11 (ALUOp2Datapath_sel[1], 1'b0, ID_lui);
  or or_12 (ALUOp2Datapath_sel[0], 1'b0, ID_ori, ID_lw, ID_sw);
  or or_13 (MemWEnable, 1'b0, ID_sw);
  or or_14 (EXTMode, 1'b0, ID_lw, ID_sw, ID_beq);
  or or_15 (Link, 1'b0, ID_jal);
  or or_16 (JumpReg, 1'b0, ID_jr);

  assign MemMode = 2'b00;

  // Other names for the same wires on the sheet: addu = ID_addu; ALUOp2Datapath_0 = ALUOp2Datapath_sel[0];
  //   ALUOp2Datapath_1 = ALUOp2Datapath_sel[1]; ALUOperation_0 = ALUOperation[0]; ALUOperation_1 = ALUOperation[1];
  //   ALUOperation_2 = ALUOperation[2]; beq = ID_beq; jal = ID_jal; jr = ID_jr; lui = ID_lui; lw = ID_lw;
  //   ori = ID_ori; subu = ID_subu; sw = ID_sw
endmodule

module Controller (
  input  [5:0] OpCode,
  input  [5:0] Funct,
  output BranchEqual,
  output Jump,
  output RegWEnable,
  output [1:0] RegWAddrpath_sel,
  output [1:0] RegWDatapath_sel,
  output [2:0] ALUOperation,
  output [1:0] ALUOp2Datapath_sel,
  output MemWEnable,
  output [1:0] MemMode,
  output EXTMode,
  output Link,
  output JumpReg
);

  wire instructiondecoder_1_id_addu, instructiondecoder_1_id_beq, instructiondecoder_1_id_jal,
       instructiondecoder_1_id_jr, instructiondecoder_1_id_lui, instructiondecoder_1_id_lw,
       instructiondecoder_1_id_ori, instructiondecoder_1_id_subu, instructiondecoder_1_id_sw;

  InstructionDecoder instructiondecoder_1 (
    .ID_addu(instructiondecoder_1_id_addu), .ID_subu(instructiondecoder_1_id_subu),
    .ID_ori(instructiondecoder_1_id_ori), .ID_lw(instructiondecoder_1_id_lw),
    .ID_sw(instructiondecoder_1_id_sw), .ID_beq(instructiondecoder_1_id_beq),
    .ID_lui(instructiondecoder_1_id_lui), .OpCode5(OpCode[5]), .OpCode4(OpCode[4]), .OpCode3(OpCode[3]),
    .OpCode2(OpCode[2]), .OpCode1(OpCode[1]), .OpCode0(OpCode[0]), .Funct5(Funct[5]), .Funct4(Funct[4]),
    .Funct3(Funct[3]), .Funct2(Funct[2]), .Funct1(Funct[1]), .Funct0(Funct[0]),
    .ID_jal(instructiondecoder_1_id_jal), .ID_jr(instructiondecoder_1_id_jr));
  ControlSignalGenerator controlsignalgenerator_1 (
    .ID_addu(instructiondecoder_1_id_addu), .BranchEqual(BranchEqual),
    .ID_subu(instructiondecoder_1_id_subu), .Jump(Jump), .ID_ori(instructiondecoder_1_id_ori),
    .RegWEnable(RegWEnable), .ID_lw(instructiondecoder_1_id_lw), .RegWAddrpath_sel(RegWAddrpath_sel),
    .ID_sw(instructiondecoder_1_id_sw), .RegWDatapath_sel(RegWDatapath_sel),
    .ID_beq(instructiondecoder_1_id_beq), .ALUOperation(ALUOperation), .ID_lui(instructiondecoder_1_id_lui),
    .ALUOp2Datapath_sel(ALUOp2Datapath_sel), .MemWEnable(MemWEnable), .MemMode(MemMode), .EXTMode(EXTMode),
    .ID_jal(instructiondecoder_1_id_jal), .Link(Link), .JumpReg(JumpReg), .ID_jr(instructiondecoder_1_id_jr));
endmodule

module CPU (
  input  reset,
  output [31:0] Instr,
  output RegWrite,
  output [4:0] RegAddr,
  output [31:0] RegData,
  output MemWrite,
  output [4:0] MemAddr,
  output [31:0] MemData
);

  wire Branch, BranchEqual, clk, EXTMode, isZero, Jump, JumpReg, Link;
  wire [1:0] ALUOp2Datapath_sel, MemMode, RegWAddrpath_sel, RegWDatapath_sel;
  wire [2:0] ALUOperation;
  wire [31:0] aluop2datapath_1_aluop2datapath_out, ALUresult, ext_1_extoutput, MemData_t, PC_4, Reg1,
       shifter_1_out;

  Clock clock_1 (.out(clk));
  IFU ifu_1 (
    .Jump(Jump), .Branch(Branch), .branchOffset(Instr[15:0]), .JAddress(Instr[25:0]), .clk(clk),
    .reset(reset), .Instr(Instr), .PC_4(PC_4), .JumpReg(JumpReg), .JRAddress(Reg1));
  DM dm_1 (
    .Address({ALUresult[31:7], MemAddr, ALUresult[1:0]}), .MemWData(MemData), .MemMode(MemMode),
    .MemRData(MemData_t), .reset(reset), .clk(clk), .MemWEnable(MemWrite));
  GRF grf_1 (
    .RAddr1(Instr[25:21]), .RAddr2(Instr[20:16]), .RegWAddr(RegAddr), .RegWData(RegData), .RD1(Reg1),
    .RD2(MemData), .clk(clk), .reset(reset), .RegWEnable(RegWrite));
  RegWAddrpath regwaddrpath_1 (
    .RegWAddrpath_rdIn(Instr[15:11]), .RegWAddrpath_rtIn(Instr[20:16]), .RegWAddrpath_out(RegAddr),
    .RegWAddrpath_sel(RegWAddrpath_sel), .RegWAddrpath_pcIn({5{1'b1}}));
  RegWDatapath regwdatapath_1 (
    .RegWDatapath_aluIn({ALUresult[31:7], MemAddr, ALUresult[1:0]}), .RegWDatapath_memIn(MemData_t),
    .RegWDatapath_out(RegData), .RegWDatapath_sel(RegWDatapath_sel), .RegWDatapath_pcIn(PC_4));
  Controller controller_1 (
    .OpCode(Instr[31:26]), .Funct(Instr[5:0]), .BranchEqual(BranchEqual), .Jump(Jump), .RegWEnable(RegWrite),
    .RegWAddrpath_sel(RegWAddrpath_sel), .RegWDatapath_sel(RegWDatapath_sel), .ALUOperation(ALUOperation),
    .ALUOp2Datapath_sel(ALUOp2Datapath_sel), .MemWEnable(MemWrite), .MemMode(MemMode), .EXTMode(EXTMode),
    .Link(Link), .JumpReg(JumpReg));
  and and_1 (Branch, isZero, BranchEqual);
  EXT ext_1 (.EXTInput(Instr[15:0]), .EXTMode(EXTMode), .EXTOutput(ext_1_extoutput));
  Shifter #(.width(32)) shifter_1 (.in(ext_1_extoutput), .\dist (5'b10000), .out(shifter_1_out));
  ALUOp2Datapath aluop2datapath_1 (
    .ALUOp2Datapath_regIn(MemData), .ALUOp2Datapath_extIn(ext_1_extoutput),
    .ALUOp2Datapath_shiftIn(shifter_1_out), .ALUOp2Datapath_out(aluop2datapath_1_aluop2datapath_out),
    .ALUOp2Datapath_sel(ALUOp2Datapath_sel));
  ALU alu_1 (
    .Operand1(Reg1), .Operand2(aluop2datapath_1_aluop2datapath_out), .ALUOperation(ALUOperation),
    .Result({ALUresult[31:7], MemAddr, ALUresult[1:0]}), .isZero(isZero));

  // Other names for the same wires on the sheet: ALUresult[6:2] = MemAddr; Address[25:0] = Instr[25:0];
  //   Funct[5:0] = Instr[5:0]; Immediate[15:0] = Instr[15:0]; shamt[4:0] = Instr[10:6]; rd[4:0] = Instr[15:11];
  //   rt[4:0] = Instr[20:16]; rs[4:0] = Instr[25:21]; OpCode[5:0] = Instr[31:26]; MemWEnable = MemWrite;
  //   Reg2[31:0] = MemData; RegWEnable = RegWrite
endmodule
